// Digital circuit 4_4bit_reg.dig as structural Verilog
module _4_4bit_reg (
  input  D_1,
  input  D_2,
  input  D_3,
  input  D_4,
  input  En,
  input  [1:0] regAddr,
  input  [2:0] Addr,
  output Q_1,
  output Q_2,
  output Q_3,
  output Q_4
);

  wire Clk_out, demultiplexer_3_out_0, demultiplexer_3_out_1, demultiplexer_3_out_2, demultiplexer_3_out_3,
       s_1, s_2, s_3, s_4, s_5, s_6, s_7, s_8;
  wire [3:0] _4_bit_regs_1_q, _4_bit_regs_2_q, _4_bit_regs_3_q, _4_bit_regs_4_q, demultiplexer_2_out_0,
       demultiplexer_2_out_1, demultiplexer_2_out_2, demultiplexer_2_out_3, driver_1_out;

  Demultiplexer #(.Selector_Bits(3)) demultiplexer_1 (
    .sel(Addr), .in(En), .out_0(s_1), .out_1(s_2), .out_2(s_3), .out_3(s_4), .out_4(s_5), .out_5(s_6),
    .out_6(s_7), .out_7(s_8));
  Button Clk (.out(Clk_out));
  assign driver_1_out = s_8 ? {D_4, D_3, D_2, D_1} : 4'bz;  // Driver driver_1
  Demultiplexer #(.Bits(4), .Selector_Bits(2)) demultiplexer_2 (
    .sel(regAddr), .in(driver_1_out), .out_0(demultiplexer_2_out_0), .out_1(demultiplexer_2_out_1),
    .out_2(demultiplexer_2_out_2), .out_3(demultiplexer_2_out_3));
  Demultiplexer #(.Selector_Bits(2)) demultiplexer_3 (
    .sel(regAddr), .in(Clk_out), .out_0(demultiplexer_3_out_0), .out_1(demultiplexer_3_out_1),
    .out_2(demultiplexer_3_out_2), .out_3(demultiplexer_3_out_3));
  _4_bit_regs _4_bit_regs_1 (.D(demultiplexer_2_out_0), .Clk(demultiplexer_3_out_0), .En(En), .Q(_4_bit_regs_1_q));
  _4_bit_regs _4_bit_regs_2 (.D(demultiplexer_2_out_1), .Clk(demultiplexer_3_out_1), .En(En), .Q(_4_bit_regs_2_q));
  _4_bit_regs _4_bit_regs_3 (.D(demultiplexer_2_out_2), .Clk(demultiplexer_3_out_2), .En(En), .Q(_4_bit_regs_3_q));
  _4_bit_regs _4_bit_regs_4 (.D(demultiplexer_2_out_3), .Clk(demultiplexer_3_out_3), .En(En), .Q(_4_bit_regs_4_q));
  assign driver_1_out = s_3 ? _4_bit_regs_3_q : 4'bz;  // Driver driver_2
  assign driver_1_out = s_1 ? _4_bit_regs_1_q : 4'bz;  // Driver driver_3
  assign driver_1_out = s_2 ? _4_bit_regs_2_q : 4'bz;  // Driver driver_4
  assign driver_1_out = s_4 ? _4_bit_regs_4_q : 4'bz;  // Driver driver_5
  Multiplexer #(.Bits(4), .Selector_Bits(2)) multiplexer_1 (
    .sel(regAddr), .in_0(_4_bit_regs_1_q), .in_1(_4_bit_regs_2_q), .in_2(_4_bit_regs_3_q),
    .in_3(_4_bit_regs_4_q), .out({Q_4, Q_3, Q_2, Q_1}));
endmodule
