// Digital circuit 4_bit_reg.dig as structural Verilog
module _4_bit_reg (
  input  D_1,
  input  D_2,
  input  D_3,
  input  D_4,
  input  Clk,
  output Q_1,
  output Q_2,
  output Q_3,
  output Q_4
);

  D_FF d_ff_1 (.D(D_1), .C(Clk), .Q(Q_1));  // open: nQ
  D_FF d_ff_2 (.D(D_2), .C(Clk), .Q(Q_2));  // open: nQ
  D_FF d_ff_3 (.D(D_3), .C(Clk), .Q(Q_3));  // open: nQ
  D_FF d_ff_4 (.D(D_4), .C(Clk), .Q(Q_4));  // open: nQ
endmodule
