// Digital circuit 4_bit_regs.dig as structural Verilog
module _4_bit_regs (
  input  [3:0] D,
  input  Clk,
  input  En,
  output [3:0] Q
);

  wire and_1_out;

  and and_1 (and_1_out, Clk, En);
  _4_bit_reg _4_bit_reg_1 (
    .D_1(D[3]), .D_2(D[2]), .D_3(D[1]), .D_4(D[0]), .Clk(and_1_out), .Q_1(Q[3]), .Q_2(Q[2]), .Q_3(Q[1]),
    .Q_4(Q[0]));
endmodule
