// Digital circuit CS3290Lab6Part5.dig as structural Verilog
module CS3290Lab6Part5 (
  input  A,
  input  B,
  input  C,
  input  In1,
  input  In2,
  input  In3,
  input  In4,
  output Out1,
  output Out2,
  output Out3,
  output Out4
);

  wire _74138_1_pin7, _74138_1_pin9, _74138_1_pin10, _74138_1_pin11, _74138_1_pin12, _74138_1_pin13,
       _74138_1_pin14, _74138_1_pin15, and_1_out, and_2_out, and_3_out, and_4_out, and_5_out, and_6_out,
       and_7_out, and_8_out, and_9_out, and_10_out, and_11_out, and_12_out, and_13_out, and_14_out,
       not_1_out, not_2_out, not_3_out, not_4_out, not_5_out, not_6_out, not_7_out, not_8_out, or_1_out,
       or_2_out, or_3_out, or_4_out, or_5_out, or_6_out, or_7_out;

  _74138 _74138_1 (
    .pin1(C), .pin2(B), .pin3(A), .pin4(1'b0), .pin5(1'b0), .pin6(1'b1), .pin7(_74138_1_pin7), .pin8(1'b0),
    .pin9(_74138_1_pin9), .pin10(_74138_1_pin10), .pin11(_74138_1_pin11), .pin12(_74138_1_pin12),
    .pin13(_74138_1_pin13), .pin14(_74138_1_pin14), .pin15(_74138_1_pin15), .pin16(1'b1));
  not not_1 (not_1_out, _74138_1_pin15);
  not not_2 (not_2_out, _74138_1_pin14);
  not not_3 (not_3_out, _74138_1_pin13);
  not not_4 (not_4_out, _74138_1_pin12);
  not not_5 (not_5_out, _74138_1_pin11);
  not not_6 (not_6_out, _74138_1_pin10);
  not not_7 (not_7_out, _74138_1_pin9);
  and and_1 (and_1_out, In1, not_1_out, _74138_1_pin7);
  and and_2 (and_2_out, In2, not_1_out, _74138_1_pin7);
  and and_3 (and_3_out, In3, not_1_out, _74138_1_pin7);
  and and_4 (and_4_out, In4, not_1_out, _74138_1_pin7);
  or or_1 (or_1_out, not_2_out, not_4_out, not_6_out);
  or or_2 (or_2_out, not_2_out, not_4_out, not_6_out);
  or or_3 (or_3_out, not_2_out, not_4_out, not_6_out);
  and and_5 (and_5_out, not_5_out, In4);
  and and_6 (and_6_out, not_7_out, In1);
  or or_4 (or_4_out, not_3_out, not_5_out, not_7_out);
  or or_5 (or_5_out, not_3_out, not_5_out, not_7_out);
  or or_6 (or_6_out, not_3_out, not_5_out, not_7_out);
  and and_7 (and_7_out, or_1_out, In2);
  and and_8 (and_8_out, or_2_out, In3);
  and and_9 (and_9_out, or_3_out, In4);
  and and_10 (and_10_out, not_4_out, In1);
  or or_7 (or_7_out, and_5_out, and_6_out);
  not not_8 (not_8_out, not_3_out);
  and and_11 (and_11_out, In1, or_4_out);
  and and_12 (and_12_out, In2, or_5_out);
  and and_13 (and_13_out, In3, or_6_out);
  and and_14 (and_14_out, or_7_out, not_8_out);
  or or_8 (Out1, and_1_out, and_7_out, and_14_out);
  or or_9 (Out2, and_2_out, and_8_out, and_11_out);
  or or_10 (Out3, and_3_out, and_9_out, and_12_out);
  or or_11 (Out4, and_4_out, and_10_out, and_13_out);
endmodule
