// Digital circuit CS3920Lab6Part4.dig as structural Verilog
module CS3920Lab6Part4 (
  input  A1,
  input  B1,
  input  C1,
  input  D1,
  input  A2,
  input  B2,
  input  C2,
  input  D2,
  input  A3,
  input  B3,
  input  C3,
  input  D3,
  input  A4,
  input  B4,
  input  C4,
  input  D4,
  output FwrtD,
  output FwrtA,
  output FwrtAB,
  output FwrtCD
);

  wire _74153_1_pin7, _74153_1_pin9, _74153_2_pin7, _74153_2_pin9, and_1_out, and_2_out, not_1_out,
       not_2_out, not_3_out, not_4_out, not_5_out, not_6_out, not_7_out, not_8_out, not_9_out, not_10_out,
       not_11_out, not_12_out, not_13_out, not_14_out, not_15_out, not_16_out, not_17_out, or_3_out,
       xor_1_out;

  not not_1 (not_1_out, A1);
  not not_2 (not_2_out, A2);
  not not_3 (not_3_out, B1);
  not not_4 (not_4_out, C1);
  not not_5 (not_5_out, B2);
  not not_6 (not_6_out, C2);
  not not_7 (not_7_out, D1);
  not not_8 (not_8_out, D2);
  _74153 _74153_1 (
    .pin1(A1), .pin2(B1), .pin3(D1), .pin4(1'b1), .pin5(not_7_out), .pin6(not_7_out), .pin7(_74153_1_pin7),
    .pin8(1'b0), .pin9(_74153_1_pin9), .pin10(D1), .pin11(D1), .pin12(1'b0), .pin13(not_7_out), .pin14(C1),
    .pin15(not_1_out), .pin16(1'b1));
  _74153 _74153_2 (
    .pin1(D2), .pin2(B2), .pin3(A2), .pin4(not_2_out), .pin5(not_2_out), .pin6(not_2_out),
    .pin7(_74153_2_pin7), .pin8(1'b0), .pin9(_74153_2_pin9), .pin10(A2), .pin11(A2), .pin12(not_2_out),
    .pin13(not_2_out), .pin14(C2), .pin15(not_8_out), .pin16(1'b1));
  or or_1 (FwrtD, _74153_1_pin9, _74153_1_pin7);
  or or_2 (FwrtA, _74153_2_pin9, _74153_2_pin7);
  not not_9 (not_9_out, A3);
  not not_10 (not_10_out, A4);
  not not_11 (not_11_out, B3);
  not not_12 (not_12_out, B4);
  not not_13 (not_13_out, D3);
  not not_14 (not_14_out, C3);
  xor xor_1 (xor_1_out, A3, B3);
  not not_15 (not_15_out, D4);
  not not_16 (not_16_out, C4);
  and and_1 (and_1_out, C4, not_15_out);
  or or_3 (or_3_out, not_16_out, and_2_out);
  and and_2 (and_2_out, C4, D4);
  not not_17 (not_17_out, xor_1_out);
  _74153 _74153_3 (
    .pin1(1'b0), .pin2(C3), .pin3(xor_1_out), .pin4(not_17_out), .pin5(xor_1_out), .pin6(not_9_out),
    .pin7(FwrtAB), .pin8(1'b0), .pin10(1'b0), .pin11(1'b0), .pin12(1'b0), .pin13(1'b0), .pin14(D3),
    .pin15(1'b1), .pin16(1'b1));  // open: pin9
  _74153 _74153_4 (
    .pin1(1'b0), .pin2(A4), .pin3(and_1_out), .pin4(D4), .pin5(or_3_out), .pin6(not_15_out), .pin7(FwrtCD),
    .pin8(1'b0), .pin10(1'b0), .pin11(1'b0), .pin12(1'b0), .pin13(1'b0), .pin14(B4), .pin15(1'b1),
    .pin16(1'b1));  // open: pin9
endmodule
