// Digital circuit Lab10Part1.dig as structural Verilog
module Lab10Part1 (
  input  clk,
  input  En
);

  wire Clr_out;
  wire [5:0] counter_1_out;
  wire [7:0] Message_d;
  wire [15:0] Alphabet_d, m_0, m_1, m_2, m_3, m_4, m_5, m_6, m_7;

  Button Clr (.out(Clr_out));
  Counter #(.Bits(6)) counter_1 (.en(En), .C(clk), .clr(Clr_out), .out(counter_1_out));  // open: ovf
  SixteenSeg sixteenseg_1 (.led(m_7), .dp(1'b0));
  ROM #(.AddrBits(6), .Bits(8)) Message (.A(counter_1_out), .sel(En), .D(Message_d));
  SixteenSeg sixteenseg_2 (.led(m_6), .dp(1'b0));
  ROM #(.AddrBits(8), .Bits(16)) Alphabet (.A(Message_d), .sel(En), .D(Alphabet_d));
  SixteenSeg sixteenseg_3 (.led(m_5), .dp(1'b0));
  Register #(.Bits(16)) Letter0 (.D(Alphabet_d), .C(clk), .en(En), .Q(m_0));
  SixteenSeg sixteenseg_4 (.led(m_4), .dp(1'b0));
  Register #(.Bits(16)) Letter1 (.D(m_0), .C(clk), .en(En), .Q(m_1));
  SixteenSeg sixteenseg_5 (.led(m_3), .dp(1'b0));
  Register #(.Bits(16)) Letter2 (.D(m_1), .C(clk), .en(En), .Q(m_2));
  SixteenSeg sixteenseg_6 (.led(m_2), .dp(1'b0));
  SixteenSeg sixteenseg_7 (.led(m_1), .dp(1'b0));
  Register #(.Bits(16)) Letter3 (.D(m_2), .C(clk), .en(En), .Q(m_3));
  SixteenSeg sixteenseg_8 (.led(m_0), .dp(1'b0));
  Register #(.Bits(16)) Letter4 (.D(m_3), .C(clk), .en(En), .Q(m_4));
  Register #(.Bits(16)) Letter5 (.D(m_4), .C(clk), .en(En), .Q(m_5));
  Register #(.Bits(16)) Letter6 (.D(m_5), .C(clk), .en(En), .Q(m_6));
  Register #(.Bits(16)) Letter7 (.D(m_6), .C(clk), .en(En), .Q(m_7));

  // Notes on the sheet:
  //   clk: Hz: 5
  //   contents of Message (hex, n*v repeats v):
  //   14,8,9,13,0,9,13,0,1,0,16,5,12,19,0,c,f,e,7,0,d,5,13,13,1,7,5
  //   ,0,14,f,0,14,5,13,14,0,14,8,9,13,0,f,15,14,10,15,14
  //   contents of Alphabet (hex, n*v repeats v):
  //   0,3cf,4a3f,f3,483f,1f3,1c3,2fb,3cc,4833,7c,31c0,f0,14cc,24cc,ff
  //   ,3c7,20ff,23c7,3bb,4803,fc,90c0,a0cc,b400,3bc,9033
endmodule
