// Digital circuit Lab10Part1Test.dig as structural Verilog
module Lab10Part1Test (
  input  En,
  input  clk
);

  wire Clr_out;
  wire [1:0] rom_1_d;
  wire [7:0] counter_1_out;
  wire [15:0] register_1_q, rom_2_d;

  Button Clr (.out(Clr_out));
  SixteenSeg sixteenseg_1 ();  // open: led, dp
  Counter #(.Bits(8)) counter_1 (.en(En), .C(clk), .clr(Clr_out), .out(counter_1_out));  // open: ovf
  ROM rom_1 (.A(counter_1_out[1:0]), .sel(En), .D(rom_1_d[0]));
  SixteenSeg sixteenseg_2 ();  // open: led, dp
  ROM rom_2 (.A(rom_1_d), .sel(En), .D(rom_2_d[0]));
  SixteenSeg sixteenseg_3 ();  // open: led, dp
  Register #(.Bits(16)) register_1 (.D(rom_2_d), .C(clk), .en(En), .Q(register_1_q));
  SixteenSeg sixteenseg_4 ();  // open: led, dp
  SixteenSeg sixteenseg_5 ();  // open: led, dp
  SixteenSeg sixteenseg_6 ();  // open: led, dp
  SixteenSeg sixteenseg_7 ();  // open: led, dp
  SixteenSeg sixteenseg_8 ();  // open: led, dp
  // Pins of 1 and 2 bits meet at rom_1_d
  // Pins of 1 and 16 bits meet at rom_2_d
  // Pins of 2 and 8 bits meet at counter_1_out
endmodule
