// Digital circuit Lab10Part2.dig as structural Verilog
module Lab10Part2 (
  input  D_1,
  input  D_2,
  input  D_3,
  input  D_4,
  input  En,
  input  [2:0] Target,
  input  [2:0] Source,
  input  A_0,
  input  A_1,
  input  A_2,
  input  A_3,
  output Q_1,
  output Q_2,
  output Q_3,
  output Q_4
);

  wire _74189_1_pin10, _74189_1_pin12, and_1_out, and_2_out, and_3_out, Clk_out, nand_1_out, not_1_out,
       not_2_out, not_3_out, s_0, s_1, s_2, s_3, s_4, s_5, s_6, s_7, T_0, T_1, T_2, T_3, T_4, T_5, T_6, T_7;
  wire [3:0] _4_bit_regs_1_q, _4_bit_regs_2_q, _4_bit_regs_3_q, _4_bit_regs_4_q, _74189_1_pin5;

  Decoder #(.Selector_Bits(3)) decoder_1 (
    .sel(Source), .out_0(s_0), .out_1(s_1), .out_2(s_2), .out_3(s_3), .out_4(s_4), .out_5(s_5), .out_6(s_6),
    .out_7(s_7));
  Decoder #(.Selector_Bits(3)) decoder_2 (
    .sel(Target), .out_0(T_0), .out_1(T_1), .out_2(T_2), .out_3(T_3), .out_4(T_4), .out_5(T_5), .out_6(T_6),
    .out_7(T_7));
  Button Clk (.out(Clk_out));
  and and_1 (and_1_out, En, Clk_out);
  not not_1 (not_1_out, T_7);
  and and_2 (and_2_out, not_1_out, s_7);
  assign {Q_4, Q_3, Q_2, Q_1} = and_2_out ? {D_4, D_3, D_2, D_1} : 4'bz;  // Driver driver_1
  _4_bit_regs _4_bit_regs_1 (.D({Q_4, Q_3, Q_2, Q_1}), .Clk(and_1_out), .En(T_0), .Q(_4_bit_regs_1_q));
  _4_bit_regs _4_bit_regs_2 (.D({Q_4, Q_3, Q_2, Q_1}), .Clk(and_1_out), .En(T_1), .Q(_4_bit_regs_2_q));
  _4_bit_regs _4_bit_regs_3 (.D({Q_4, Q_3, Q_2, Q_1}), .Clk(and_1_out), .En(T_2), .Q(_4_bit_regs_3_q));
  _4_bit_regs _4_bit_regs_4 (.D({Q_4, Q_3, Q_2, Q_1}), .Clk(and_1_out), .En(T_3), .Q(_4_bit_regs_4_q));
  assign {Q_4, Q_3, Q_2, Q_1} = s_0 ? _4_bit_regs_1_q : 4'bz;  // Driver driver_2
  assign {Q_4, Q_3, Q_2, Q_1} = s_1 ? _4_bit_regs_2_q : 4'bz;  // Driver driver_3
  assign {Q_4, Q_3, Q_2, Q_1} = s_2 ? _4_bit_regs_3_q : 4'bz;  // Driver driver_4
  assign {Q_4, Q_3, Q_2, Q_1} = s_3 ? _4_bit_regs_4_q : 4'bz;  // Driver driver_5
  assign {Q_4, Q_3, Q_2, Q_1} = and_3_out ? _74189_1_pin5 : 4'bz;  // Driver driver_6
  and and_3 (and_3_out, T_7, s_7);
  nand nand_1 (nand_1_out, T_7, and_1_out);
  not not_2 (not_2_out, D_1);
  not not_3 (not_3_out, D_2);
  _74189 _74189_1 (
    .pin1(A_0), .pin2(1'b0), .pin3(nand_1_out), .pin4(not_2_out), .pin5(_74189_1_pin5[0]), .pin6(not_3_out),
    .pin7(_74189_1_pin5[1]), .pin8(1'b0), .pin9(_74189_1_pin5[2]), .pin10(_74189_1_pin10),
    .pin11(_74189_1_pin5[3]), .pin12(_74189_1_pin12), .pin13(A_3), .pin14(A_2), .pin15(A_1), .pin16(1'b1));
  not not_4 (_74189_1_pin12, D_4);
  not not_5 (_74189_1_pin10, D_3);

  // Other names for the same wires on the sheet: D_0 = D_1; D_1_t = D_2; D_2_t = D_3; D_3_t = D_4
endmodule
