// Digital circuit Lab11Part1.dig as structural Verilog
module Lab11Part1 (
  input  D_0,
  input  D_1,
  input  D_2,
  input  D_3,
  input  En,
  input  [2:0] Target,
  input  [2:0] Source,
  input  Address_0,
  input  Address_1,
  input  Address_2,
  input  Address_3,
  input  Shift_0,
  input  Shift_1,
  input  Shift_2,
  input  AddSubSwitch,
  output Q_0,
  output Q_1,
  output Q_2,
  output Q_3
);

  wire _74189_1_pin10, _74189_1_pin12, and_1_out, Clk_out, nand_1_out, not_1_out, not_2_out, s_0, s_1, s_2,
       s_3, s_4, s_5, s_6, s_7, T_0, T_1, T_2, T_3, T_4, T_5, T_6, T_7;
  wire [3:0] _4_bit_regs_1_q, _4_bit_regs_2_q, _4_bit_regs_3_q, _4_bit_regs_4_q, _74189_1_pin5, A, B,
       cs3290lab6part5_1_out1, lab4_1_f0;

  Decoder #(.Selector_Bits(3)) decoder_1 (
    .sel(Source), .out_0(s_0), .out_1(s_1), .out_2(s_2), .out_3(s_3), .out_4(s_4), .out_5(s_5), .out_6(s_6),
    .out_7(s_7));
  Decoder #(.Selector_Bits(3)) decoder_2 (
    .sel(Target), .out_0(T_0), .out_1(T_1), .out_2(T_2), .out_3(T_3), .out_4(T_4), .out_5(T_5), .out_6(T_6),
    .out_7(T_7));
  Button Clk (.out(Clk_out));
  and and_1 (and_1_out, En, Clk_out);
  assign {Q_3, Q_2, Q_1, Q_0} = s_7 ? {D_3, D_2, D_1, D_0} : 4'bz;  // Driver driver_1
  _4_bit_regs _4_bit_regs_1 (.D({Q_3, Q_2, Q_1, Q_0}), .Clk(and_1_out), .En(T_0), .Q(_4_bit_regs_1_q));
  _4_bit_regs _4_bit_regs_2 (.D({Q_3, Q_2, Q_1, Q_0}), .Clk(and_1_out), .En(T_1), .Q(_4_bit_regs_2_q));
  _4_bit_regs _4_bit_regs_3 (.D({Q_3, Q_2, Q_1, Q_0}), .Clk(and_1_out), .En(T_2), .Q(_4_bit_regs_3_q));
  _4_bit_regs _4_bit_regs_4 (.D({Q_3, Q_2, Q_1, Q_0}), .Clk(and_1_out), .En(T_3), .Q(_4_bit_regs_4_q));
  _4_bit_regs _4_bit_regs_5 (.D({Q_3, Q_2, Q_1, Q_0}), .Clk(and_1_out), .En(T_6), .Q(A));
  _4_bit_regs _4_bit_regs_6 (.D({Q_3, Q_2, Q_1, Q_0}), .Clk(and_1_out), .En(T_7), .Q(B));
  CS3290Lab6Part5 cs3290lab6part5_1 (
    .A(Shift_2), .B(Shift_1), .C(Shift_0), .In1(A[0]), .In2(A[1]), .In3(A[2]), .In4(A[3]),
    .Out1(cs3290lab6part5_1_out1[0]), .Out2(cs3290lab6part5_1_out1[1]), .Out3(cs3290lab6part5_1_out1[2]),
    .Out4(cs3290lab6part5_1_out1[3]));
  lab4 lab4_1 (
    .B1(B[1]), .A1(A[1]), .B0(B[0]), .A0(A[0]), .B3(B[3]), .A3(A[3]), .B2(B[2]), .A2(A[2]),
    .AddSubSwitch(AddSubSwitch), .F0(lab4_1_f0[0]), .F1(lab4_1_f0[1]), .F2(lab4_1_f0[2]), .F3(lab4_1_f0[3]));  // open: Fcarry
  assign {Q_3, Q_2, Q_1, Q_0} = s_0 ? _4_bit_regs_1_q : 4'bz;  // Driver driver_2
  assign {Q_3, Q_2, Q_1, Q_0} = s_1 ? _4_bit_regs_2_q : 4'bz;  // Driver driver_3
  assign {Q_3, Q_2, Q_1, Q_0} = s_2 ? _4_bit_regs_3_q : 4'bz;  // Driver driver_4
  assign {Q_3, Q_2, Q_1, Q_0} = s_3 ? _4_bit_regs_4_q : 4'bz;  // Driver driver_5
  assign {Q_3, Q_2, Q_1, Q_0} = s_5 ? cs3290lab6part5_1_out1 : 4'bz;  // Driver driver_6
  assign {Q_3, Q_2, Q_1, Q_0} = s_6 ? lab4_1_f0 : 4'bz;  // Driver driver_7
  assign {Q_3, Q_2, Q_1, Q_0} = s_4 ? _74189_1_pin5 : 4'bz;  // Driver driver_8
  nand nand_1 (nand_1_out, T_4, and_1_out);
  not not_1 (not_1_out, Q_0);
  not not_2 (not_2_out, Q_1);
  _74189 _74189_1 (
    .pin1(Address_0), .pin2(1'b0), .pin3(nand_1_out), .pin4(not_1_out), .pin5(_74189_1_pin5[0]),
    .pin6(not_2_out), .pin7(_74189_1_pin5[1]), .pin8(1'b0), .pin9(_74189_1_pin5[2]), .pin10(_74189_1_pin10),
    .pin11(_74189_1_pin5[3]), .pin12(_74189_1_pin12), .pin13(Address_3), .pin14(Address_2),
    .pin15(Address_1), .pin16(1'b1));
  not not_3 (_74189_1_pin12, Q_3);
  not not_4 (_74189_1_pin10, Q_2);

  // Other names for the same wires on the sheet: A_0 = A[0]; A_1 = A[1]; A_2 = A[2]; A_3 = A[3]; B_0 = B[0];
  //   B_1 = B[1]; B_2 = B[2]; B_3 = B[3]; D_0_t = Q_0; Data[3:0] = {Q_3, Q_2, Q_1, Q_0}; D_1_t = Q_1; D_2_t = Q_2;
  //   D_3_t = Q_3
endmodule
