// Digital circuit Lab7.dig as structural Verilog
module Lab7 (
  input  In1,
  input  CLK,
  input  Serial,
  input  Switch,
  input  In2,
  input  In3,
  input  In4,
  output Out1,
  output Out2,
  output Out3,
  output Out4
);

  wire d_ff_1_p3, d_ff_2_p3, d_ff_3_p3, d_ff_4_p3, d_ff_5_p3, d_ff_6_p3, d_ff_7_p3, d_ff_8_p3;

  // D_FF d_ff_1: pin names not known; wires that end beside it: In1, CLK, d_ff_1_p3
  // D_FF d_ff_2: pin names not known; wires that end beside it: Serial, CLK, d_ff_2_p3
  Multiplexer multiplexer_1 (.sel(Switch), .in_0(d_ff_1_p3), .in_1(d_ff_2_p3), .out(Out1));
  // D_FF d_ff_3: pin names not known; wires that end beside it: In2, CLK, d_ff_3_p3
  // D_FF d_ff_4: pin names not known; wires that end beside it: d_ff_2_p3, CLK, d_ff_4_p3
  Multiplexer multiplexer_2 (.sel(Switch), .in_0(d_ff_3_p3), .in_1(d_ff_4_p3), .out(Out2));
  // D_FF d_ff_5: pin names not known; wires that end beside it: In3, CLK, d_ff_5_p3
  // D_FF d_ff_6: pin names not known; wires that end beside it: d_ff_4_p3, CLK, d_ff_6_p3
  Multiplexer multiplexer_3 (.sel(Switch), .in_0(d_ff_5_p3), .in_1(d_ff_6_p3), .out(Out3));
  // D_FF d_ff_7: pin names not known; wires that end beside it: In4, CLK, d_ff_7_p3
  // D_FF d_ff_8: pin names not known; wires that end beside it: d_ff_6_p3, CLK, d_ff_8_p3
  Multiplexer multiplexer_4 (.sel(Switch), .in_0(d_ff_7_p3), .in_1(d_ff_8_p3), .out(Out4));
endmodule
