// Digital circuit Lab8Part3.dig as structural Verilog
module Lab8Part3 (
  input  X,
  input  Clr,
  output Y,
  output Q_A,
  output Q_B
);

  wire and_1_out, and_2_out, Clk_out, jk_ff_as_1_nq, not_1_out, or_1_out, xor_1_out;

  not not_1 (not_1_out, X);
  Button Clk (.out(Clk_out));
  or or_1 (or_1_out, Q_A, X);
  and and_1 (and_1_out, not_1_out, Q_B);
  xor xor_1 (xor_1_out, Q_A, X);
  and and_2 (and_2_out, Q_A, X);
  JK_FF_AS jk_ff_as_1 (.Set(1'b0), .J(or_1_out), .C(Clk_out), .K(and_1_out), .Clr(Clr), .Q(Q_A), .nQ(jk_ff_as_1_nq));
  JK_FF_AS jk_ff_as_2 (.Set(1'b0), .J(xor_1_out), .C(Clk_out), .K(and_2_out), .Clr(Clr), .Q(Q_B));  // open: nQ
  and and_3 (Y, jk_ff_as_1_nq, not_1_out, Q_B);

  // Other names for the same wires on the sheet: A = Q_A
endmodule
