// Digital circuit Lab8Part5.dig as structural Verilog
module Lab8Part5 (
  input  D_1,
  input  D_2,
  input  D_3,
  input  D_4,
  input  [1:0] Addr,
  input  En,
  output O_1,
  output O_2,
  output O_3,
  output O_4
);

  wire Clk, Clk_A, Clk_B, Clk_C, Clk_D, demultiplexer_2_out_0, demultiplexer_2_out_1, demultiplexer_2_out_2,
       demultiplexer_2_out_3, demultiplexer_3_out_0, demultiplexer_3_out_1, demultiplexer_3_out_2,
       demultiplexer_3_out_3, demultiplexer_4_out_0, demultiplexer_4_out_1, demultiplexer_4_out_2,
       demultiplexer_4_out_3, demultiplexer_5_out_0, demultiplexer_5_out_1, demultiplexer_5_out_2,
       demultiplexer_5_out_3, I_A1, I_A2, I_A3, I_A4, I_B1, I_B2, I_B3, I_B4, I_C1, I_C2, I_C3, I_C4, I_D1,
       I_D2, I_D3, I_D4, O_A1, O_A2, O_A3, O_A4, O_B1, O_B2, O_B3, O_B4, O_C1, O_C2, O_C3, O_C4, O_D1, O_D2,
       O_D3, O_D4;

  Demultiplexer #(.Selector_Bits(2)) demultiplexer_1 (
    .sel(Addr), .in(Clk), .out_0(Clk_A), .out_1(Clk_B), .out_2(Clk_C), .out_3(Clk_D));
  Demultiplexer #(.Selector_Bits(2)) demultiplexer_2 (
    .sel(Addr), .in(D_1), .out_0(demultiplexer_2_out_0), .out_1(demultiplexer_2_out_1),
    .out_2(demultiplexer_2_out_2), .out_3(demultiplexer_2_out_3));
  Demultiplexer #(.Selector_Bits(2)) demultiplexer_3 (
    .sel(Addr), .in(D_2), .out_0(demultiplexer_3_out_0), .out_1(demultiplexer_3_out_1),
    .out_2(demultiplexer_3_out_2), .out_3(demultiplexer_3_out_3));
  Demultiplexer #(.Selector_Bits(2)) demultiplexer_4 (
    .sel(Addr), .in(D_3), .out_0(demultiplexer_4_out_0), .out_1(demultiplexer_4_out_1),
    .out_2(demultiplexer_4_out_2), .out_3(demultiplexer_4_out_3));
  Demultiplexer #(.Selector_Bits(2)) demultiplexer_5 (
    .sel(Addr), .in(D_4), .out_0(demultiplexer_5_out_0), .out_1(demultiplexer_5_out_1),
    .out_2(demultiplexer_5_out_2), .out_3(demultiplexer_5_out_3));
  Multiplexer multiplexer_1 (.sel(En), .in_0(O_A2), .in_1(demultiplexer_3_out_0), .out(I_A2));
  Multiplexer multiplexer_2 (.sel(En), .in_0(O_B2), .in_1(demultiplexer_3_out_1), .out(I_B2));
  Multiplexer multiplexer_3 (.sel(En), .in_0(O_C2), .in_1(demultiplexer_3_out_2), .out(I_C2));
  Multiplexer multiplexer_4 (.sel(En), .in_0(O_D2), .in_1(demultiplexer_3_out_3), .out(I_D2));
  Multiplexer multiplexer_5 (.sel(En), .in_0(O_A3), .in_1(demultiplexer_4_out_0), .out(I_A3));
  Multiplexer multiplexer_6 (.sel(En), .in_0(O_B3), .in_1(demultiplexer_4_out_1), .out(I_B3));
  Multiplexer multiplexer_7 (.sel(En), .in_0(O_C3), .in_1(demultiplexer_4_out_2), .out(I_C3));
  Multiplexer multiplexer_8 (.sel(En), .in_0(O_D3), .in_1(demultiplexer_4_out_3), .out(I_D3));
  Multiplexer multiplexer_9 (.sel(En), .in_0(O_A4), .in_1(demultiplexer_5_out_0), .out(I_A4));
  Multiplexer multiplexer_10 (.sel(En), .in_0(O_B4), .in_1(demultiplexer_5_out_1), .out(I_B4));
  Multiplexer multiplexer_11 (.sel(En), .in_0(O_C4), .in_1(demultiplexer_5_out_2), .out(I_C4));
  Multiplexer multiplexer_12 (.sel(En), .in_0(O_D4), .in_1(demultiplexer_5_out_3), .out(I_D4));
  Multiplexer multiplexer_13 (.sel(En), .in_0(O_A1), .in_1(demultiplexer_2_out_0), .out(I_A1));
  Multiplexer multiplexer_14 (.sel(En), .in_0(O_B1), .in_1(demultiplexer_2_out_1), .out(I_B1));
  Multiplexer multiplexer_15 (.sel(En), .in_0(O_C1), .in_1(demultiplexer_2_out_2), .out(I_C1));
  Multiplexer multiplexer_16 (.sel(En), .in_0(O_D1), .in_1(demultiplexer_2_out_3), .out(I_D1));
  D_FF d_ff_1 (.D(I_A1), .C(Clk_A), .Q(O_A1));  // open: nQ
  D_FF d_ff_2 (.D(I_A2), .C(Clk_A), .Q(O_A2));  // open: nQ
  D_FF d_ff_3 (.D(I_A3), .C(Clk_A), .Q(O_A3));  // open: nQ
  D_FF d_ff_4 (.D(I_A4), .C(Clk_A), .Q(O_A4));  // open: nQ
  D_FF d_ff_5 (.D(I_B1), .C(Clk_B), .Q(O_B1));  // open: nQ
  D_FF d_ff_6 (.D(I_B2), .C(Clk_B), .Q(O_B2));  // open: nQ
  D_FF d_ff_7 (.D(I_B3), .C(Clk_B), .Q(O_B3));  // open: nQ
  D_FF d_ff_8 (.D(I_B4), .C(Clk_B), .Q(O_B4));  // open: nQ
  D_FF d_ff_9 (.D(I_C1), .C(Clk_C), .Q(O_C1));  // open: nQ
  D_FF d_ff_10 (.D(I_C2), .C(Clk_C), .Q(O_C2));  // open: nQ
  D_FF d_ff_11 (.D(I_C3), .C(Clk_C), .Q(O_C3));  // open: nQ
  D_FF d_ff_12 (.D(I_C4), .C(Clk_C), .Q(O_C4));  // open: nQ
  D_FF d_ff_13 (.D(I_D1), .C(Clk_D), .Q(O_D1));  // open: nQ
  D_FF d_ff_14 (.D(I_D2), .C(Clk_D), .Q(O_D2));  // open: nQ
  D_FF d_ff_15 (.D(I_D3), .C(Clk_D), .Q(O_D3));  // open: nQ
  D_FF d_ff_16 (.D(I_D4), .C(Clk_D), .Q(O_D4));  // open: nQ
  Button u_Clk (.out(Clk));
  Multiplexer #(.Selector_Bits(2)) multiplexer_17 (
    .sel(Addr), .in_0(O_A1), .in_1(O_B1), .in_2(O_C1), .in_3(O_D1), .out(O_1));
  Multiplexer #(.Selector_Bits(2)) multiplexer_18 (
    .sel(Addr), .in_0(O_A2), .in_1(O_B2), .in_2(O_C2), .in_3(O_D2), .out(O_2));
  Multiplexer #(.Selector_Bits(2)) multiplexer_19 (
    .sel(Addr), .in_0(O_A3), .in_1(O_B3), .in_2(O_C3), .in_3(O_D3), .out(O_3));
  Multiplexer #(.Selector_Bits(2)) multiplexer_20 (
    .sel(Addr), .in_0(O_A4), .in_1(O_B4), .in_2(O_C4), .in_3(O_D4), .out(O_4));

  // Other names for the same wires on the sheet: I_1 = D_1; I_2 = D_2; I_3 = D_3; I_4 = D_4
endmodule
