// Digital circuit Lab9_Part3.dig as structural Verilog
module Lab9_Part3 (
  input  X_1,
  input  X_2,
  output Y
);

  wire A, and_1_out, and_2_out, and_3_out, B, Clk_out, Clr_out, J_A, J_B, K_A, nA, nB, not_1_out, not_2_out,
       not_3_out, not_4_out, xnor_1_out;

  not not_1 (not_1_out, X_1);
  and and_1 (and_1_out, A, nB, not_1_out);
  not not_2 (not_2_out, X_2);
  xnor xnor_1 (xnor_1_out, A, X_1);
  Button Clk (.out(Clk_out));
  Button Clr (.out(Clr_out));
  and and_2 (and_2_out, A, B);
  and and_3 (and_3_out, A, nB, X_1, not_2_out);
  not not_3 (not_3_out, X_1);
  and and_4 (J_A, nA, B, not_3_out, X_2);
  or or_1 (K_A, and_2_out, and_1_out, and_3_out);
  and and_5 (J_B, nB, xnor_1_out, X_2);
  JK_FF_AS jk_ff_as_1 (.Set(1'b0), .J(J_A), .C(Clk_out), .K(K_A), .Clr(Clr_out), .Q(A), .nQ(nA));
  JK_FF_AS jk_ff_as_2 (.Set(1'b0), .J(J_B), .C(Clk_out), .K(1'b1), .Clr(Clr_out), .Q(B), .nQ(nB));
  not not_4 (not_4_out, X_2);
  and and_6 (Y, A, B, X_1, not_4_out);
endmodule
