// Digital circuit lab4.dig as structural Verilog
module lab4 (
  input  B1,
  input  A1,
  input  B0,
  input  A0,
  input  B3,
  input  A3,
  input  B2,
  input  A2,
  input  AddSubSwitch,
  output F0,
  output F1,
  output F2,
  output F3,
  output Fcarry
);

  wire add_1_c_o, add_2_c_o, add_3_c_o, add_4_c_o, xor_1_out, xor_2_out, xor_3_out, xor_4_out;

  xor xor_1 (xor_1_out, B0, AddSubSwitch);
  Add add_1 (.a(A0), .b(xor_1_out), .c_i(AddSubSwitch), .s(F0), .c_o(add_1_c_o));
  xor xor_2 (xor_2_out, AddSubSwitch, B1);
  xor xor_3 (xor_3_out, AddSubSwitch, B2);
  xor xor_4 (xor_4_out, B3, AddSubSwitch);
  Add add_2 (.a(A1), .b(xor_2_out), .c_i(add_1_c_o), .s(F1), .c_o(add_2_c_o));
  Add add_3 (.a(A2), .b(xor_3_out), .c_i(add_2_c_o), .s(F2), .c_o(add_3_c_o));
  Add add_4 (.a(A3), .b(xor_4_out), .c_i(add_3_c_o), .s(F3), .c_o(add_4_c_o));
  xor xor_5 (Fcarry, add_4_c_o, AddSubSwitch);
endmodule
